// Logisim project main.circ as structural Verilog: 6 circuits, main circuit main
module main (
  output [39:0] out_1,
  output [7:0] out_2,
  output [3:0] out_3,
  output [3:0] out_4,
  output [15:0] out_5,
  output [15:0] out_6,
  output [8:0] out_7
);

  wire ALLOW_WRITE, and_2_out, and_4_out, and_6_out, and_7_out, ARG1_POINTER, ARG1_TYPE, ARG2_POINTER,
       ARG2_TYPE, CLK, clock_1_out, comparator_1_eq, d_ff_1_q, demultiplexer_1_out0, demultiplexer_1_out1,
       demultiplexer_1_out2, demultiplexer_1_out3, demultiplexer_1_out4, demultiplexer_1_out5,
       demultiplexer_1_out6, demultiplexer_1_out7, demultiplexer_2_out0, demultiplexer_2_out1,
       demultiplexer_3_out2, demultiplexer_4_out1, FLAG_VALUE, HALT, MEM_WE, not_1_out, not_2_out, not_3_out,
       not_4_out, or_2_out, or_3_out, or_4_out, RESET, STOP_VIDEO, VIDEO_REFRESH, X_POS_carry;
  wire [2:0] bit_extender_1_out, bit_extender_2_out;
  wire [5:0] rgb_video_1_p5, X_POS_q;
  wire [8:0] counter_1_q;
  wire [15:0] adder_1_out, adder_2_out, ADDR_MEM, ARG1_REG_VALUE, ARG2_REG_VALUE, bit_extender_3_out,
       bit_extender_4_out, divider_1_out, get_addr_target_1_out_4, get_addr_target_2_out_4,
       multiplexer_4_out, multiplexer_5_out, multiplexer_6_out, multiplexer_8_out, multiplier_1_out,
       multiplier_2_out, R0_q, R1_q, R2_q, R3_q, R4_q, R5_q, R6_q, R7_q, RES_OPERATOR, SAVE_VALUE,
       subtractor_1_out, VALUE_MEM_Q, VIDEO_ADDR;

  Clock clock_1 (.out(clock_1_out));
  Button button_1 (.out(RESET));
  and and_1 (CLK, clock_1_out, ~HALT);  // AND_Gate
  not not_1 (not_1_out, CLK);
  Adder #(.width(16)) adder_1 (.a(ARG1_REG_VALUE), .b(ARG2_REG_VALUE), .out(adder_1_out));  // open: cin, cout
  Subtractor #(.width(16)) subtractor_1 (
    .a(ARG1_REG_VALUE), .b(ARG2_REG_VALUE), .out(subtractor_1_out));  // open: bin, bout
  Multiplier #(.width(16)) multiplier_1 (
    .a(ARG1_REG_VALUE), .b(ARG2_REG_VALUE), .out(multiplier_1_out));  // open: cin, cout
  Divider #(.width(16)) divider_1 (.a(ARG1_REG_VALUE), .b(ARG2_REG_VALUE), .out(divider_1_out));  // open: upper, rem
  is_memaddr is_memaddr_1 (.INT_ARG(out_1[31:16]), .out_2(ARG1_TYPE));
  is_memaddr is_memaddr_2 (.INT_ARG(out_1[15:0]), .out_2(ARG2_TYPE));
  Comparator #(.width(4)) comparator_1 (.a(out_1[39:36]), .b(4'b0100), .eq(comparator_1_eq));  // open: gt, lt
  and and_2 (and_2_out, ~VIDEO_REFRESH, not_1_out);  // AND_Gate
  or or_1 (MEM_WE, ARG1_TYPE, ARG1_POINTER);
  Multiplexer #(.select(2), .width(16)) multiplexer_1 (
    .in0(adder_1_out), .in1(subtractor_1_out), .in2(multiplier_1_out), .in3(divider_1_out),
    .out(RES_OPERATOR), .sel(out_1[33:32]));
  Counter #(.max('h1ff), .width(9)) counter_1 (
    .clr(RESET), .load(FLAG_VALUE), .clk(and_2_out), .D(out_1[24:16]), .Q(counter_1_q));  // open: up, count, carry
  is_pointer is_pointer_1 (.REG_ARG(out_1[31:16]), .IS_MEMADDR(ARG1_TYPE), .out_3(ARG1_POINTER));
  is_pointer is_pointer_2 (.REG_ARG(out_1[15:0]), .IS_MEMADDR(ARG2_TYPE), .out_3(ARG2_POINTER));
  D_Flip_Flop d_ff_1 (.D(comparator_1_eq), .clk(CLK), .Q(d_ff_1_q), .reset(or_2_out));  // open: Qn, preset
  or or_2 (or_2_out, RESET, STOP_VIDEO);
  condition condition_1 (
    .RST(RESET), .CLOCK(CLK), .INT_TYPE1(out_1[39:36]), .INT_TYPE2(out_1[35:32]),
    .ARG1_VALUE(ARG1_REG_VALUE), .ARG2_VALUE(ARG2_REG_VALUE), .RES(FLAG_VALUE));
  and and_3 (VIDEO_REFRESH, d_ff_1_q, ~STOP_VIDEO);  // AND_Gate
  ROM #(.addrWidth(9), .dataWidth(40)) PROG (.addr(counter_1_q), .data(out_1));
  Demultiplexer #(.select(3)) demultiplexer_1 (
    .out0(demultiplexer_1_out0), .out1(demultiplexer_1_out1), .out2(demultiplexer_1_out2),
    .out3(demultiplexer_1_out3), .out4(demultiplexer_1_out4), .out5(demultiplexer_1_out5),
    .out6(demultiplexer_1_out6), .out7(demultiplexer_1_out7), .in(1'b1), .sel(out_1[18:16]));
  Comparator comparator_2 (.a(out_1[39:32]), .b({8{1'b1}}), .eq(HALT));  // open: gt, lt
  Demultiplexer #(.select(2)) demultiplexer_2 (
    .out0(demultiplexer_2_out0), .out1(demultiplexer_2_out1), .in(1'b1), .sel(out_1[37:36]));  // open: out2, out3
  and and_4 (and_4_out, ~ARG1_TYPE, ~ARG1_POINTER, ALLOW_WRITE);  // AND_Gate
  Register #(.trigger("high"), .width(16)) R0 (
    .D(SAVE_VALUE), .en(demultiplexer_1_out0), .clk(and_4_out), .Q(R0_q), .clr(RESET));
  Register #(.trigger("high"), .width(16)) R1 (
    .D(SAVE_VALUE), .en(demultiplexer_1_out1), .clk(and_4_out), .Q(R1_q), .clr(RESET));
  Register #(.trigger("high"), .width(16)) R2 (
    .D(SAVE_VALUE), .en(demultiplexer_1_out2), .clk(and_4_out), .Q(R2_q), .clr(RESET));
  Register #(.trigger("high"), .width(16)) R3 (
    .D(SAVE_VALUE), .en(demultiplexer_1_out3), .clk(and_4_out), .Q(R3_q), .clr(RESET));
  Register #(.trigger("high"), .width(16)) R4 (
    .D(SAVE_VALUE), .en(demultiplexer_1_out4), .clk(and_4_out), .Q(R4_q), .clr(RESET));
  Register #(.trigger("high"), .width(16)) R5 (
    .D(SAVE_VALUE), .en(demultiplexer_1_out5), .clk(and_4_out), .Q(R5_q), .clr(RESET));
  Register #(.trigger("high"), .width(16)) R6 (
    .D(SAVE_VALUE), .en(demultiplexer_1_out6), .clk(and_4_out), .Q(R6_q), .clr(RESET));
  Register #(.trigger("high"), .width(16)) R7 (
    .D(SAVE_VALUE), .en(demultiplexer_1_out7), .clk(and_4_out), .Q(R7_q), .clr(RESET));
  or or_3 (or_3_out, demultiplexer_2_out0, demultiplexer_2_out1);
  Multiplexer #(.select(3), .width(16)) multiplexer_2 (
    .in0(R0_q), .in1(R1_q), .in2(R2_q), .in3(R3_q), .in4(R4_q), .in5(R5_q), .in6(R6_q), .in7(R7_q),
    .out(ARG1_REG_VALUE), .sel(bit_extender_1_out));
  Multiplexer #(.select(3), .width(16)) multiplexer_3 (
    .in0(R0_q), .in1(R1_q), .in2(R2_q), .in3(R3_q), .in4(R4_q), .in5(R5_q), .in6(R6_q), .in7(R7_q),
    .out(ARG2_REG_VALUE), .sel(bit_extender_2_out));
  and and_5 (ALLOW_WRITE, or_3_out, CLK);
  Bit_Extender #(.in_width(16), .out_width(3)) bit_extender_1 (.in(out_1[31:16]), .out(bit_extender_1_out));
  or or_4 (or_4_out, ARG2_TYPE, ARG2_POINTER);
  Bit_Extender #(.in_width(16), .out_width(3)) bit_extender_2 (.in(out_1[15:0]), .out(bit_extender_2_out));
  RAM #(.addrWidth(16), .dataWidth(16)) MEMORY (
    .addr(ADDR_MEM), .we(MEM_WE), .oe(1'b1), .clk(CLK), .din(SAVE_VALUE), .dout(VALUE_MEM_Q));
  get_addr_target get_addr_target_1 (
    .INT_ARG(out_1[15:0]), .REG_VALUE(ARG2_REG_VALUE), .IS_POINTER(ARG2_POINTER),
    .out_4(get_addr_target_1_out_4));
  get_addr_target get_addr_target_2 (
    .INT_ARG(out_1[31:16]), .REG_VALUE(ARG1_REG_VALUE), .IS_POINTER(ARG1_POINTER),
    .out_4(get_addr_target_2_out_4));
  Multiplexer #(.width(16)) multiplexer_4 (
    .in0(ARG2_REG_VALUE), .in1(VALUE_MEM_Q), .out(multiplexer_4_out), .sel(or_4_out));
  Demultiplexer #(.select(2)) demultiplexer_3 (
    .out2(demultiplexer_3_out2), .in(1'b1), .sel(out_1[33:32]));  // open: out0, out1, out3
  Demultiplexer #(.select(2)) demultiplexer_4 (
    .out1(demultiplexer_4_out1), .in(1'b1), .sel(out_1[37:36]));  // open: out0, out2, out3
  Multiplexer #(.width(16)) multiplexer_5 (
    .in0(get_addr_target_1_out_4), .in1(get_addr_target_2_out_4), .out(multiplexer_5_out), .sel(MEM_WE));
  Multiplexer #(.width(16)) multiplexer_6 (
    .in0(multiplexer_4_out), .in1(out_1[15:0]), .out(multiplexer_6_out), .sel(demultiplexer_3_out2));
  Multiplexer #(.width(16)) multiplexer_7 (
    .in0(multiplexer_5_out), .in1(VIDEO_ADDR), .out(ADDR_MEM), .sel(VIDEO_REFRESH));
  // Probe on VALUE_MEM_Q
  Register #(.trigger("low"), .width(16)) register_1 (
    .D(multiplexer_8_out), .en(not_2_out), .clk(CLK), .Q(SAVE_VALUE));  // open: clr
  Multiplexer #(.width(16)) multiplexer_8 (
    .in0(multiplexer_6_out), .in1(RES_OPERATOR), .out(multiplexer_8_out), .sel(demultiplexer_4_out1));
  not not_2 (not_2_out, CLK);
  not not_3 (not_3_out, CLK);
  not not_4 (not_4_out, VIDEO_REFRESH);
  and and_6 (and_6_out, VIDEO_REFRESH, not_3_out);
  Counter #(.max('h3f), .trigger("falling"), .width(6)) X_POS (
    .Q(X_POS_q), .carry(X_POS_carry), .clk(and_6_out), .clr(not_4_out));  // open: load, D, count, up
  // RGB_Video #(.cursor("No Cursor"), .height(64), .scale(6), .width(64)) rgb_video_1: pin names not known; wires that end beside it: RESET, CLK, VIDEO_REFRESH, X_POS_q, rgb_video_1_p5, VALUE_MEM_Q[14:0]
  Counter #(.max('h3f), .trigger("falling"), .width(6)) Y_POS (
    .Q(rgb_video_1_p5), .clk(and_7_out), .clr(not_4_out));  // open: load, D, count, carry, up
  and and_7 (and_7_out, and_6_out, X_POS_carry);
  assign bit_extender_3_out = {{10{1'b0}}, rgb_video_1_p5};  // Bit_Extender bit_extender_3
  assign bit_extender_4_out = {{10{1'b0}}, X_POS_q};  // Bit_Extender bit_extender_4
  Multiplier #(.width(16)) multiplier_2 (
    .a(16'h40), .b(bit_extender_3_out), .out(multiplier_2_out));  // open: cin, cout
  Adder #(.width(16)) adder_2 (.a(multiplier_2_out), .b(bit_extender_4_out), .out(adder_2_out));  // open: cin, cout
  Adder #(.width(16)) adder_3 (.a(adder_2_out), .b(16'hf000), .out(VIDEO_ADDR));  // open: cin, cout
  Comparator #(.width(16)) comparator_3 (.a(VIDEO_ADDR), .b({16{1'b1}}), .eq(STOP_VIDEO));  // open: gt, lt

  assign out_2 = out_1[39:32];
  assign out_3 = out_1[39:36];
  assign out_4 = out_1[35:32];
  assign out_5 = out_1[31:16];
  assign out_6 = out_1[15:0];

  // Other names for the same wires on the sheet: INT_ARG2[15:0] = out_1[15:0]; INT_BITFIELD[39:0] = out_1;
  //   INT_ARG1[15:0] = out_1[31:16]; INT_OP_TYPE2[3:0] = out_1[35:32]; INT_OPCODE[7:0] = out_1[39:32];
  //   INT_OP_TYPE1[3:0] = out_1[39:36]; INT_COUNTER[8:0] = out_7

  // Notes on the sheet:
  //   <Ctrl-R> is better
  //   contents of PROG (hex, n*v repeats v):
  //   200000005 200010009 200020009 200030000 2100030000 2000000001 2000020000 2000010002 ff00000000
endmodule

module is_memaddr (
  input  [15:0] INT_ARG,
  output out_2
);

  wire comparator_1_eq, comparator_1_gt;

  Comparator #(.width(16)) comparator_1 (
    .a(INT_ARG), .b(16'h20), .gt(comparator_1_gt), .eq(comparator_1_eq));  // open: lt
  or or_1 (out_2, comparator_1_gt, comparator_1_eq);
endmodule

module is_pointer (
  input  [15:0] REG_ARG,
  input  IS_MEMADDR,
  output out_3
);

  and and_1 (out_3, REG_ARG[4], ~IS_MEMADDR);  // AND_Gate
endmodule

module get_addr_target (
  input  [15:0] INT_ARG,
  input  [15:0] REG_VALUE,
  input  IS_POINTER,
  output [15:0] out_4
);

  Multiplexer #(.width(16)) multiplexer_1 (.in0(INT_ARG), .in1(REG_VALUE), .out(out_4), .sel(IS_POINTER));
endmodule

module condition (
  input  RST,
  input  CLOCK,
  input  [3:0] INT_TYPE1,
  input  [3:0] INT_TYPE2,
  input  [15:0] ARG1_VALUE,
  input  [15:0] ARG2_VALUE,
  output RES
);

  wire and_1_out, and_2_out, and_3_out, and_4_out, and_6_out, BEQ_q, BEQ_qn, BGT_q, BLT_q, comparator_1_eq,
       comparator_2_eq, comparator_2_gt, comparator_2_lt, comparator_3_eq, demultiplexer_1_out0,
       demultiplexer_1_out1, demultiplexer_1_out2, demultiplexer_1_out3, demultiplexer_1_out4, or_1_out;
  wire [15:0] multiplexer_1_out;

  Multiplexer #(.width(16)) multiplexer_1 (
    .in0(ARG2_VALUE), .in1({16{1'b0}}), .out(multiplexer_1_out), .sel(INT_TYPE2[0]));
  Comparator #(.width(4)) comparator_1 (.a(INT_TYPE1), .b(4'b0010), .eq(comparator_1_eq));  // open: gt, lt
  and and_1 (and_1_out, comparator_1_eq, CLOCK);
  Comparator #(.mode("unsigned"), .width(16)) comparator_2 (
    .a(ARG1_VALUE), .b(multiplexer_1_out), .gt(comparator_2_gt), .eq(comparator_2_eq), .lt(comparator_2_lt));
  D_Flip_Flop BGT (.D(comparator_2_gt), .clk(and_1_out), .Q(BGT_q), .reset(RST));  // open: Qn, preset
  D_Flip_Flop BEQ (.D(comparator_2_eq), .clk(and_1_out), .Q(BEQ_q), .Qn(BEQ_qn), .reset(RST));  // open: preset
  D_Flip_Flop BLT (.D(comparator_2_lt), .clk(and_1_out), .Q(BLT_q), .reset(RST));  // open: Qn, preset
  Demultiplexer #(.select(4)) demultiplexer_1 (
    .out0(demultiplexer_1_out0), .out1(demultiplexer_1_out1), .out2(demultiplexer_1_out2),
    .out3(demultiplexer_1_out3), .out4(demultiplexer_1_out4), .in(1'b1), .sel(INT_TYPE2));  // open: out5, out6, out7, out8, out9, out10, out11, out12, out13, out14, out15
  and and_2 (and_2_out, demultiplexer_1_out3, BGT_q);
  or or_1 (or_1_out, demultiplexer_1_out4, and_2_out, and_3_out, and_4_out, and_6_out);
  Comparator #(.width(2)) comparator_3 (.a(INT_TYPE1[1:0]), .b(2'b11), .eq(comparator_3_eq));  // open: gt, lt
  and and_3 (and_3_out, demultiplexer_1_out2, BLT_q);
  and and_4 (and_4_out, demultiplexer_1_out1, BEQ_qn);
  and and_5 (RES, or_1_out, comparator_3_eq);
  and and_6 (and_6_out, demultiplexer_1_out0, BEQ_q);
endmodule

module alu (
  input  [15:0] ARG1_VALUE,
  input  [15:0] ARG2_VALUE,
  input  [3:0] INT_TYPE2,
  output [15:0] RES
);

  wire [3:0] bit_extender_1_out;
  wire [15:0] adder_1_out, and_1_out, divider_1_out, multiplier_1_out, not_1_out, or_1_out, shifter_1_out,
       shifter_2_out, subtractor_1_out, xor_1_out;

  Adder #(.width(16)) adder_1 (.a(ARG1_VALUE), .b(ARG2_VALUE), .out(adder_1_out));  // open: cin, cout
  Subtractor #(.width(16)) subtractor_1 (.a(ARG1_VALUE), .b(ARG2_VALUE), .out(subtractor_1_out));  // open: bin, bout
  Multiplier #(.width(16)) multiplier_1 (.a(ARG1_VALUE), .b(ARG2_VALUE), .out(multiplier_1_out));  // open: cin, cout
  Divider #(.width(16)) divider_1 (.a(ARG1_VALUE), .b(ARG2_VALUE), .out(divider_1_out));  // open: upper, rem
  assign not_1_out = ~ARG1_VALUE;  // NOT_Gate not_1, 16 bits wide
  assign and_1_out = ARG1_VALUE & ARG2_VALUE;  // AND_Gate and_1, 16 bits wide
  assign or_1_out = ARG1_VALUE | ARG2_VALUE;  // OR_Gate or_1, 16 bits wide
  assign xor_1_out = ARG1_VALUE ^ ARG2_VALUE;  // XOR_Gate xor_1, 16 bits wide
  Bit_Extender #(.in_width(16), .out_width(4), .\type ("zero")) bit_extender_1 (
    .in(ARG2_VALUE), .out(bit_extender_1_out));
  Shifter #(.shift("rl"), .width(16)) shifter_1 (.in(ARG1_VALUE), .\dist (bit_extender_1_out), .out(shifter_1_out));
  Shifter #(.shift("rr"), .width(16)) shifter_2 (.in(ARG1_VALUE), .\dist (bit_extender_1_out), .out(shifter_2_out));
  Multiplexer #(.select(4), .width(16)) multiplexer_1 (
    .in0(adder_1_out), .in1(subtractor_1_out), .in2(multiplier_1_out), .in3(divider_1_out), .in4(not_1_out),
    .in5(and_1_out), .in6(or_1_out), .in7(xor_1_out), .in8(shifter_1_out), .in9(shifter_2_out), .out(RES),
    .sel(INT_TYPE2));  // open: in10, in11, in12, in13, in14, in15
endmodule
